// Logisim project project3.circ as structural Verilog: 4 circuits, main circuit regfile
module CPU (
);

  wire alu_1_equal, and_1_out, and_2_out, clock_1_out, control_1_beqsel, control_1_bnesel, control_1_immsel,
       control_1_jalrsel, control_1_jalsel, control_1_jrsel, control_1_jsel, control_1_lwsel,
       control_1_regwritee, control_1_shiftsel, control_1_swsel, not_1_out, or_1_out, or_2_out, or_3_out,
       or_4_out, or_5_out;
  wire [3:0] control_1_alucode;
  wire [4:0] control_1_rd, control_1_rs, control_1_rt;
  wire [15:0] bit_extender_1_out, bit_extender_2_out;
  wire [31:0] adder_1_out, adder_2_out, alu_1_res, control_1_imm, control_1_shiftamount, multiplexer_1_out,
       multiplexer_2_out, multiplexer_3_out, multiplexer_4_out, multiplexer_5_out, multiplexer_6_out,
       regfile_1_rs_data, regfile_1_rt_data, register_1_q, rom_1_data, shifter_1_out, shifter_2_out,
       shifter_3_out, shifter_4_out;

  Adder #(.width(32)) adder_1 (.a(register_1_q), .b(32'h4), .out(adder_1_out));  // open: cin, cout
  Shifter #(.width(32)) shifter_1 (.in(control_1_imm), .\dist (5'b00010), .out(shifter_1_out));
  Adder #(.width(32)) adder_2 (.a(adder_1_out), .b(shifter_1_out), .out(adder_2_out));  // open: cin, cout
  Shifter #(.width(32)) shifter_2 (.in(control_1_imm), .\dist (5'b00010), .out(shifter_2_out));
  Multiplexer #(.width(32)) multiplexer_1 (
    .in0(adder_1_out), .in1(adder_2_out), .out(multiplexer_1_out), .sel(or_3_out));
  Multiplexer #(.width(32)) multiplexer_2 (
    .in0(shifter_2_out), .in1(regfile_1_rs_data), .out(multiplexer_2_out), .sel(or_1_out));
  Register #(.width(32)) register_1 (.D(multiplexer_3_out), .Q(register_1_q));  // open: en, clk, clr
  Multiplexer #(.width(32)) multiplexer_3 (
    .in0(multiplexer_1_out), .in1(multiplexer_2_out), .out(multiplexer_3_out), .sel(or_2_out));
  Shifter #(.shift("lr"), .width(32)) shifter_3 (.in(register_1_q), .\dist (5'b00010), .out(shifter_3_out));
  Bit_Extender #(.in_width(32)) bit_extender_1 (.in(shifter_3_out), .out(bit_extender_1_out));
  ROM #(.addrWidth(16), .dataWidth(32)) rom_1 (.addr(bit_extender_1_out), .data(rom_1_data));
  Multiplexer #(.width(32)) multiplexer_4 (.in0(alu_1_res), .in1(adder_1_out), .out(multiplexer_4_out), .sel(or_4_out));
  or or_1 (or_1_out, control_1_jrsel, control_1_jalrsel);
  or or_2 (or_2_out, control_1_jalsel, control_1_jsel, control_1_jalrsel, control_1_jrsel);
  regfile regfile_1 (
    .rd_data(multiplexer_4_out), .write_e(control_1_regwritee), .rt(control_1_rt), .rs(control_1_rs),
    .rd(control_1_rd), .rs_data(regfile_1_rs_data), .rt_data(regfile_1_rt_data));
  or or_3 (or_3_out, and_1_out, and_2_out);
  Control control_1 (
    .Inst(rom_1_data), .ALUCode(control_1_alucode), .jrSel(control_1_jrsel), .jalrSel(control_1_jalrsel),
    .shiftSel(control_1_shiftsel), .shiftAmount(control_1_shiftamount), .rd(control_1_rd), .rt(control_1_rt),
    .rs(control_1_rs), .imm(control_1_imm), .lwSel(control_1_lwsel), .swSel(control_1_swsel),
    .beqSel(control_1_beqsel), .bneSel(control_1_bnesel), .immSel(control_1_immsel), .jSel(control_1_jsel),
    .jalSel(control_1_jalsel), .regWriteE(control_1_regwritee));
  Multiplexer #(.width(32)) multiplexer_5 (
    .in0(regfile_1_rt_data), .in1(control_1_imm), .out(multiplexer_5_out), .sel(control_1_immsel));
  and and_1 (and_1_out, control_1_bnesel, not_1_out);
  and and_2 (and_2_out, alu_1_equal, control_1_beqsel);
  Multiplexer #(.width(32)) multiplexer_6 (
    .in0(regfile_1_rs_data), .in1(control_1_shiftamount), .out(multiplexer_6_out), .sel(control_1_shiftsel));
  not not_1 (not_1_out, alu_1_equal);
  or or_4 (or_4_out, control_1_jalrsel, control_1_jalsel);
  ALU alu_1 (
    .op2(multiplexer_5_out), .op1(multiplexer_6_out), .ALUCode(control_1_alucode), .res(alu_1_res),
    .equal(alu_1_equal));
  Shifter #(.shift("lr"), .width(32)) shifter_4 (.in(alu_1_res), .\dist (5'b11110), .out(shifter_4_out));
  Bit_Extender #(.in_width(32)) bit_extender_2 (.in(shifter_4_out), .out(bit_extender_2_out));
  or or_5 (or_5_out, control_1_swsel, control_1_lwsel);
  RAM #(.addrWidth(16), .dataWidth(32), .enables("line")) ram_1 (
    .addr(bit_extender_2_out), .we(or_5_out), .clk(clock_1_out));  // open: din, dout
  Clock clock_1 (.out(clock_1_out));

  // Notes on the sheet:
  //   offset
  //   pc+4
  //   offset
  //   rd_data
  //   branchSelect
  //   branchSelect
  //   jSelect
  //   ProgramCounter
  //   jr/jalr
  //   j-type
  //   branch
  //   immSel
  //   bne
  //   beq
  //   shiftSel
  //   jalr/jal
endmodule

module regfile (
  input  [31:0] rd_data,
  input  [4:0] rd,
  input  write_e,
  input  [4:0] rs,
  input  [4:0] rt,
  output [31:0] rs_data,
  output [31:0] rt_data
);

  wire and_1_out, clock_1_out, demultiplexer_1_out0, demultiplexer_1_out1, demultiplexer_1_out2,
       demultiplexer_1_out3, demultiplexer_1_out4, demultiplexer_1_out5, demultiplexer_1_out6,
       demultiplexer_1_out7, demultiplexer_1_out8, demultiplexer_1_out9, demultiplexer_1_out10,
       demultiplexer_1_out11, demultiplexer_1_out12, demultiplexer_1_out13, demultiplexer_1_out14,
       demultiplexer_1_out15, demultiplexer_1_out16, demultiplexer_1_out17, demultiplexer_1_out18,
       demultiplexer_1_out19, demultiplexer_1_out20, demultiplexer_1_out21, demultiplexer_1_out22,
       demultiplexer_1_out23, demultiplexer_1_out24, demultiplexer_1_out25, demultiplexer_1_out26,
       demultiplexer_1_out27, demultiplexer_1_out28, demultiplexer_1_out29, demultiplexer_1_out30,
       demultiplexer_1_out31;
  wire [31:0] R0_q, R1_q, R2_q, R3_q, R4_q, R5_q, R6_q, R7_q, R8_q, R9_q, R10_q, R11_q, R12_q, R13_q, R14_q,
       R15_q, R16_q, R17_q, R18_q, R19_q, R20_q, R21_q, R22_q, R23_q, R24_q, R25_q, R26_q, R27_q, R28_q,
       R29_q, R30_q, R31_q;

  Clock clock_1 (.out(clock_1_out));
  Demultiplexer #(.select(5)) demultiplexer_1 (
    .out0(demultiplexer_1_out0), .out1(demultiplexer_1_out1), .out2(demultiplexer_1_out2),
    .out3(demultiplexer_1_out3), .out4(demultiplexer_1_out4), .out5(demultiplexer_1_out5),
    .out6(demultiplexer_1_out6), .out7(demultiplexer_1_out7), .out8(demultiplexer_1_out8),
    .out9(demultiplexer_1_out9), .out10(demultiplexer_1_out10), .out11(demultiplexer_1_out11),
    .out12(demultiplexer_1_out12), .out13(demultiplexer_1_out13), .out14(demultiplexer_1_out14),
    .out15(demultiplexer_1_out15), .out16(demultiplexer_1_out16), .out17(demultiplexer_1_out17),
    .out18(demultiplexer_1_out18), .out19(demultiplexer_1_out19), .out20(demultiplexer_1_out20),
    .out21(demultiplexer_1_out21), .out22(demultiplexer_1_out22), .out23(demultiplexer_1_out23),
    .out24(demultiplexer_1_out24), .out25(demultiplexer_1_out25), .out26(demultiplexer_1_out26),
    .out27(demultiplexer_1_out27), .out28(demultiplexer_1_out28), .out29(demultiplexer_1_out29),
    .out30(demultiplexer_1_out30), .out31(demultiplexer_1_out31), .in(write_e), .sel(rd));
  Register #(.width(32)) R1 (.D(rd_data), .en(demultiplexer_1_out1), .clk(clock_1_out), .Q(R1_q));  // open: clr
  Register #(.width(32)) R2 (.D(rd_data), .en(demultiplexer_1_out2), .clk(clock_1_out), .Q(R2_q));  // open: clr
  Register #(.width(32)) R3 (.D(rd_data), .en(demultiplexer_1_out3), .clk(clock_1_out), .Q(R3_q));  // open: clr
  Register #(.width(32)) R4 (.D(rd_data), .en(demultiplexer_1_out4), .clk(clock_1_out), .Q(R4_q));  // open: clr
  Register #(.width(32)) R5 (.D(rd_data), .en(demultiplexer_1_out5), .clk(clock_1_out), .Q(R5_q));  // open: clr
  Register #(.width(32)) R6 (.D(rd_data), .en(demultiplexer_1_out6), .clk(clock_1_out), .Q(R6_q));  // open: clr
  Register #(.width(32)) R7 (.D(rd_data), .en(demultiplexer_1_out7), .clk(clock_1_out), .Q(R7_q));  // open: clr
  Register #(.width(32)) R8 (.D(rd_data), .en(demultiplexer_1_out8), .clk(clock_1_out), .Q(R8_q));  // open: clr
  Register #(.width(32)) R9 (.D(rd_data), .en(demultiplexer_1_out9), .clk(clock_1_out), .Q(R9_q));  // open: clr
  Register #(.width(32)) R10 (.D(rd_data), .en(demultiplexer_1_out10), .clk(clock_1_out), .Q(R10_q));  // open: clr
  Register #(.width(32)) R11 (.D(rd_data), .en(demultiplexer_1_out11), .clk(clock_1_out), .Q(R11_q));  // open: clr
  Register #(.width(32)) R12 (.D(rd_data), .en(demultiplexer_1_out12), .clk(clock_1_out), .Q(R12_q));  // open: clr
  Register #(.width(32)) R13 (.D(rd_data), .en(demultiplexer_1_out13), .clk(clock_1_out), .Q(R13_q));  // open: clr
  Register #(.width(32)) R14 (.D(rd_data), .en(demultiplexer_1_out14), .clk(clock_1_out), .Q(R14_q));  // open: clr
  Register #(.width(32)) R15 (.D(rd_data), .en(demultiplexer_1_out15), .clk(clock_1_out), .Q(R15_q));  // open: clr
  Register #(.width(32)) R16 (.D(rd_data), .en(demultiplexer_1_out16), .clk(clock_1_out), .Q(R16_q));  // open: clr
  Register #(.width(32)) R17 (.D(rd_data), .en(demultiplexer_1_out17), .clk(clock_1_out), .Q(R17_q));  // open: clr
  Register #(.width(32)) R18 (.D(rd_data), .en(demultiplexer_1_out18), .clk(clock_1_out), .Q(R18_q));  // open: clr
  Register #(.width(32)) R19 (.D(rd_data), .en(demultiplexer_1_out19), .clk(clock_1_out), .Q(R19_q));  // open: clr
  Register #(.width(32)) R20 (.D(rd_data), .en(demultiplexer_1_out20), .clk(clock_1_out), .Q(R20_q));  // open: clr
  Register #(.width(32)) R21 (.D(rd_data), .en(demultiplexer_1_out21), .clk(clock_1_out), .Q(R21_q));  // open: clr
  Register #(.width(32)) R22 (.D(rd_data), .en(demultiplexer_1_out22), .clk(clock_1_out), .Q(R22_q));  // open: clr
  Register #(.width(32)) R23 (.D(rd_data), .en(demultiplexer_1_out23), .clk(clock_1_out), .Q(R23_q));  // open: clr
  Register #(.width(32)) R24 (.D(rd_data), .en(demultiplexer_1_out24), .clk(clock_1_out), .Q(R24_q));  // open: clr
  Register #(.width(32)) R25 (.D(rd_data), .en(demultiplexer_1_out25), .clk(clock_1_out), .Q(R25_q));  // open: clr
  Register #(.width(32)) R26 (.D(rd_data), .en(demultiplexer_1_out26), .clk(clock_1_out), .Q(R26_q));  // open: clr
  Register #(.width(32)) R27 (.D(rd_data), .en(demultiplexer_1_out27), .clk(clock_1_out), .Q(R27_q));  // open: clr
  Register #(.width(32)) R28 (.D(rd_data), .en(demultiplexer_1_out28), .clk(clock_1_out), .Q(R28_q));  // open: clr
  Register #(.width(32)) R29 (.D(rd_data), .en(demultiplexer_1_out29), .clk(clock_1_out), .Q(R29_q));  // open: clr
  Register #(.width(32)) R30 (.D(rd_data), .en(demultiplexer_1_out30), .clk(clock_1_out), .Q(R30_q));  // open: clr
  and and_1 (and_1_out, demultiplexer_1_out0, 1'b0);
  Register #(.width(32)) R31 (.D(rd_data), .en(demultiplexer_1_out31), .clk(clock_1_out), .Q(R31_q));  // open: clr
  Register #(.width(32)) R0 (.D(rd_data), .en(and_1_out), .clk(clock_1_out), .Q(R0_q));  // open: clr
  Multiplexer #(.select(5), .width(32)) multiplexer_1 (
    .in0(R0_q), .in1(R1_q), .in2(R2_q), .in3(R3_q), .in4(R4_q), .in5(R5_q), .in6(R6_q), .in7(R7_q),
    .in8(R8_q), .in9(R9_q), .in10(R10_q), .in11(R11_q), .in12(R12_q), .in13(R13_q), .in14(R14_q),
    .in15(R15_q), .in16(R16_q), .in17(R17_q), .in18(R18_q), .in19(R19_q), .in20(R20_q), .in21(R21_q),
    .in22(R22_q), .in23(R23_q), .in24(R24_q), .in25(R25_q), .in26(R26_q), .in27(R27_q), .in28(R28_q),
    .in29(R29_q), .in30(R30_q), .in31(R31_q), .out(rs_data), .sel(rs));
  Multiplexer #(.select(5), .width(32)) multiplexer_2 (
    .in0(R0_q), .in1(R1_q), .in2(R2_q), .in3(R3_q), .in4(R4_q), .in5(R5_q), .in6(R6_q), .in7(R7_q),
    .in8(R8_q), .in9(R9_q), .in10(R10_q), .in11(R11_q), .in12(R12_q), .in13(R13_q), .in14(R14_q),
    .in15(R15_q), .in16(R16_q), .in17(R17_q), .in18(R18_q), .in19(R19_q), .in20(R20_q), .in21(R21_q),
    .in22(R22_q), .in23(R23_q), .in24(R24_q), .in25(R25_q), .in26(R26_q), .in27(R27_q), .in28(R28_q),
    .in29(R29_q), .in30(R30_q), .in31(R31_q), .out(rt_data), .sel(rt));
endmodule

module ALU (
  input  [3:0] ALUCode,
  input  [31:0] op1,
  input  [31:0] op2,
  output [31:0] res,
  output equal
);

  wire clock_1_out, clock_2_out, comparator_2_lt, comparator_3_eq, comparator_3_gt, or_1_out;
  wire [4:0] bit_extender_1_out, bit_extender_2_out;
  wire [31:0] adder_1_out, bit_extender_3_out, divider_1_out, divider_1_rem, HI_q, LO_q, multiplexer_1_out,
       multiplexer_2_out, multiplier_1_cout, multiplier_1_out, shifter_1_out, shifter_2_out, subtractor_1_out;

  Comparator #(.width(32)) comparator_1 (.a(op1), .b(op2), .eq(equal));  // open: gt, lt
  Adder #(.width(32)) adder_1 (.a(op1), .b(op2), .out(adder_1_out));  // open: cin, cout
  Subtractor #(.width(32)) subtractor_1 (.a(op1), .b(op2), .out(subtractor_1_out));  // open: bin, bout
  Divider #(.width(32)) divider_1 (.a(op1), .b(op2), .out(divider_1_out), .rem(divider_1_rem));  // open: upper
  Multiplier #(.width(32)) multiplier_1 (
    .a(op1), .b(op2), .out(multiplier_1_out), .cout(multiplier_1_cout));  // open: cin
  Bit_Extender #(.in_width(32), .out_width(5)) bit_extender_1 (.in(op1), .out(bit_extender_1_out));
  Bit_Extender #(.in_width(32), .out_width(5)) bit_extender_2 (.in(op1), .out(bit_extender_2_out));
  Comparator #(.width(32)) comparator_2 (.a(op1), .b(op2), .lt(comparator_2_lt));  // open: gt, eq
  Shifter #(.width(32)) shifter_1 (.in(op2), .\dist (bit_extender_1_out), .out(shifter_1_out));
  Shifter #(.shift("lr"), .width(32)) shifter_2 (.in(op2), .\dist (bit_extender_2_out), .out(shifter_2_out));
  Comparator #(.mode("unsigned"), .width(4)) comparator_3 (
    .a(ALUCode), .b(4'b1000), .gt(comparator_3_gt), .eq(comparator_3_eq));  // open: lt
  or or_1 (or_1_out, comparator_3_eq, comparator_3_gt);
  assign bit_extender_3_out = {{31{1'b0}}, comparator_2_lt};  // Bit_Extender bit_extender_3
  Multiplexer #(.width(32)) multiplexer_1 (
    .in0(multiplier_1_out), .in1(divider_1_out), .out(multiplexer_1_out), .sel(comparator_3_gt));
  Multiplexer #(.width(32)) multiplexer_2 (
    .in0(multiplier_1_cout), .in1(divider_1_rem), .out(multiplexer_2_out), .sel(comparator_3_gt));
  Register #(.width(32)) LO (.D(multiplexer_1_out), .en(or_1_out), .clk(clock_1_out), .Q(LO_q));  // open: clr
  Clock clock_1 (.out(clock_1_out));
  Register #(.width(32)) HI (.D(multiplexer_2_out), .en(or_1_out), .clk(clock_2_out), .Q(HI_q));  // open: clr
  Clock clock_2 (.out(clock_2_out));
  Multiplexer #(.select(4), .width(32)) multiplexer_3 (
    .in0(adder_1_out), .in1(subtractor_1_out), .in2(LO_q), .in3(HI_q), .in4(shifter_1_out),
    .in5(shifter_2_out), .in7(bit_extender_3_out), .out(res), .sel(ALUCode));  // open: in6, in8, in9, in10, in11, in12, in13, in14, in15

  // Notes on the sheet:
  //   op2 only
  //   add
  //   sub
  //   div
  //   mult
  //   sll
  //   srl
endmodule

module Control (
  input  [31:0] Inst,
  output [3:0] ALUCode,
  output jrSel,
  output jalrSel,
  output shiftSel,
  output [31:0] shiftAmount,
  output [4:0] rd,
  output [4:0] rt,
  output [4:0] rs,
  output [31:0] imm,
  output lwSel,
  output swSel,
  output beqSel,
  output bneSel,
  output immSel,
  output jSel,
  output jalSel,
  output regWriteE
);

  wire comparator_1_eq, comparator_2_eq, comparator_9_eq, comparator_11_eq, comparator_12_eq,
       comparator_13_eq, comparator_14_eq, comparator_15_eq, comparator_16_eq, comparator_17_eq,
       comparator_18_eq, comparator_19_eq, comparator_20_eq, or_1_out, or_2_out, or_4_out, or_5_out, or_7_out;
  wire [4:0] multiplexer_2_out, multiplexer_13_out;
  wire [5:0] multiplexer_1_out;
  wire [31:0] bit_extender_2_out;

  Comparator #(.width(6)) comparator_1 (.a(Inst[31:26]), .b({6{1'b0}}), .eq(comparator_1_eq));  // open: gt, lt
  Multiplexer #(.width(6)) multiplexer_1 (
    .in0(6'b001111), .in1(Inst[5:0]), .out(multiplexer_1_out), .sel(comparator_1_eq));
  Comparator #(.width(6)) comparator_2 (.a(Inst[31:26]), .b(6'b001000), .eq(comparator_2_eq));  // open: gt, lt
  Comparator #(.width(6)) comparator_3 (.a(Inst[31:26]), .b(6'b100011), .eq(lwSel));  // open: gt, lt
  Comparator #(.width(6)) comparator_4 (.a(Inst[31:26]), .b(6'b101011), .eq(swSel));  // open: gt, lt
  Comparator #(.width(6)) comparator_5 (.a(Inst[31:26]), .b(6'b000100), .eq(beqSel));  // open: gt, lt
  Comparator #(.width(6)) comparator_6 (.a(Inst[31:26]), .b(6'b000101), .eq(bneSel));  // open: gt, lt
  Comparator #(.width(6)) comparator_7 (.a(Inst[31:26]), .b(6'b000010), .eq(jSel));  // open: gt, lt
  Comparator #(.width(6)) comparator_8 (.a(Inst[31:26]), .b(6'b000011), .eq(jalSel));  // open: gt, lt
  Comparator #(.width(6)) comparator_9 (.a(multiplexer_1_out), .b(6'b001100), .eq(comparator_9_eq));  // open: gt, lt
  Comparator #(.width(6)) comparator_10 (.a(multiplexer_1_out), .b(6'b001000), .eq(jrSel));  // open: gt, lt
  Comparator #(.width(6)) comparator_11 (.a(multiplexer_1_out), .b(6'b001001), .eq(comparator_11_eq));  // open: gt, lt
  Comparator #(.width(6)) comparator_12 (.a(multiplexer_1_out), .b(6'b101010), .eq(comparator_12_eq));  // open: gt, lt
  Comparator #(.width(6)) comparator_13 (.a(multiplexer_1_out), .b(6'b010010), .eq(comparator_13_eq));  // open: gt, lt
  Comparator #(.width(6)) comparator_14 (.a(multiplexer_1_out), .b(6'b010000), .eq(comparator_14_eq));  // open: gt, lt
  Comparator #(.width(6)) comparator_15 (.a(multiplexer_1_out), .b({6{1'b0}}), .eq(comparator_15_eq));  // open: gt, lt
  Comparator #(.width(6)) comparator_16 (.a(multiplexer_1_out), .b(6'b000010), .eq(comparator_16_eq));  // open: gt, lt
  Comparator #(.width(6)) comparator_17 (.a(multiplexer_1_out), .b(6'b011000), .eq(comparator_17_eq));  // open: gt, lt
  Comparator #(.width(6)) comparator_18 (.a(multiplexer_1_out), .b(6'b011010), .eq(comparator_18_eq));  // open: gt, lt
  Comparator #(.width(6)) comparator_19 (.a(multiplexer_1_out), .b(6'b100000), .eq(comparator_19_eq));  // open: gt, lt
  Comparator #(.width(6)) comparator_20 (.a(multiplexer_1_out), .b(6'b100010), .eq(comparator_20_eq));  // open: gt, lt
  Multiplexer #(.width(5)) multiplexer_2 (
    .in0(Inst[15:11]), .in1(Inst[20:16]), .out(multiplexer_2_out), .sel(or_1_out));
  or or_1 (or_1_out, comparator_2_eq, lwSel);
  or or_2 (or_2_out, jSel, jalSel);
  or or_3 (shiftSel, comparator_15_eq, comparator_16_eq);
  or or_4 (or_4_out, comparator_17_eq, comparator_18_eq);
  Multiplexer #(.width(4)) multiplexer_3 (.in1(4'b0111), .out(ALUCode), .sel(comparator_12_eq));  // open: in0
  Multiplexer #(.width(4)) multiplexer_4 (.in1(4'b0010), .out(ALUCode), .sel(comparator_13_eq));  // open: in0
  Multiplexer #(.width(4)) multiplexer_5 (.in1(4'b0011), .out(ALUCode), .sel(comparator_14_eq));  // open: in0
  Multiplexer #(.width(4)) multiplexer_6 (.in1(4'b0100), .out(ALUCode), .sel(comparator_15_eq));  // open: in0
  Multiplexer #(.width(4)) multiplexer_7 (.in1(4'b0101), .out(ALUCode), .sel(comparator_16_eq));  // open: in0
  Multiplexer #(.width(4)) multiplexer_8 (.in1(4'b1000), .out(ALUCode), .sel(comparator_17_eq));  // open: in0
  Multiplexer #(.width(4)) multiplexer_9 (.in1(4'b1001), .out(ALUCode), .sel(comparator_18_eq));  // open: in0
  Multiplexer #(.width(4)) multiplexer_10 (.in1(4'b0000), .out(ALUCode), .sel(comparator_19_eq));  // open: in0
  Multiplexer #(.width(4)) multiplexer_11 (.in1(4'b0001), .out(ALUCode), .sel(comparator_20_eq));  // open: in0
  Multiplexer #(.width(4)) multiplexer_12 (.in1(4'b0000), .out(ALUCode), .sel(comparator_2_eq));  // open: in0
  or or_5 (or_5_out, swSel, beqSel, bneSel, jSel);
  or or_6 (jalrSel, comparator_9_eq, comparator_11_eq);
  or or_7 (or_7_out, or_4_out, or_5_out);
  assign shiftAmount = {{27{Inst[10]}}, Inst[10:6]};  // Bit_Extender bit_extender_1
  not not_1 (regWriteE, or_7_out);
  or or_8 (immSel, jalrSel, lwSel, swSel, comparator_2_eq, jalSel);
  Multiplexer #(.width(5)) multiplexer_13 (
    .in0(multiplexer_2_out), .in1({5{1'b1}}), .out(multiplexer_13_out), .sel(jalSel));
  assign bit_extender_2_out = {{16{Inst[15]}}, Inst[15:0]};  // Bit_Extender bit_extender_2
  Multiplexer #(.width(5)) multiplexer_14 (.in0(multiplexer_13_out), .in1(5'b11010), .out(rd), .sel(comparator_9_eq));
  Multiplexer #(.width(32)) multiplexer_15 (
    .in0(bit_extender_2_out), .in1({{6{1'b0}}, Inst[25:0]}), .out(imm), .sel(or_2_out));

  assign rs = Inst[25:21];
  assign rt = Inst[20:16];

  // Notes on the sheet:
  //   addi
  //   lw
  //   sw
  //   beq
  //   bne
  //   j
  //   jal
  //   syscall
  //   jr
  //   jalr
  //   slt
  //   mflo
  //   mfhi
  //   sll
  //   srl
  //   mult
  //   div
  //   add
  //   sub
endmodule
